# Fritzing sketch tia20005563 (saved by Fritzing 0.9.9b)
breadboards: 1

parts:
  R1 = Resistor [tolerance=±5% power=0.25 resistance=220 package=THT]
  R2 = Resistor [tolerance=±5% power=0.25 resistance=220 package=THT]
  R3 = Resistor [tolerance=±5% power=0.25 resistance=220 package=THT]
  R4 = Resistor [tolerance=±5% power=0.25 resistance=220 package=THT]
  RHT1 = Humidity and Temperature Sensor RHT03
  U1 = NodeMCU V1.0
  LED1 = LEDs [package=led10mm]
  LED2 = LEDs [package=led10mm]
  LED3 = LEDs [package=led10mm]
  LED4 = LEDs [package=led10mm]
  RHT2 = Humidity and Temperature Sensor RHT03
  M1 = Keyes l9110 Fan module [package=THT]

nets:
  N1: R1.Pin_0, R2.Pin_0, R3.Pin_0, R4.Pin_0, RHT1.GND_2, U1.GND
  N2: R1.Pin_1, LED1.C
  N3: R2.Pin_1, LED4.C
  N4: R3.Pin_1, LED3.C
  N5: R4.Pin_1, LED2.C
  VCC: RHT1.Vcc, U1.3V3
  N6: U1.D5, LED2.A
  N7: RHT2.Vcc, M1.pin1
  N8: RHT2.Data-signal, M1.pin2
  N9: RHT2.GND_1, M1.pin3
  N10: RHT2.GND_2, M1.pin4

custom parts:
  NodeMCU V1.0: ESP8266 based NodeMCU
  Keyes l9110 Fan module: Keyes l9110 Fan module. Done from pictures without an actual board to hand so breadboard may not be fully accurate.
